# Fritzing sketch StepperMotor (saved by Fritzing 0.8.7b)
breadboards: 1

parts:
  FRDM-KL25Z1 = FRDM-KL25Z [part_number=FRDM-KL25Z]
  Componente1 = Breadboard Power Supply Board SMD
  MOTOR1 = 28BYJ-48 Stepper Motor
  BREAKOUT1 = ULN2003A breakout board

nets:
  N1: FRDM-KL25Z1.D8_PTA13, BREAKOUT1.In_4
  N2: FRDM-KL25Z1.D9_PTD5_PWM, BREAKOUT1.In_3
  N3: FRDM-KL25Z1.D10_PTD0_PWM, BREAKOUT1.In_2
  N4: FRDM-KL25Z1.D11_PTD2_PWM, BREAKOUT1.In_1
  GND: FRDM-KL25Z1.GND, FRDM-KL25Z1.GND2, Componente1.GND, BREAKOUT1.0V
  VCC: Componente1.VCC, BREAKOUT1.+5V
  N5: MOTOR1.RED, BREAKOUT1.RED_wire
  N6: MOTOR1.ORANGE, BREAKOUT1.ORANGE_wire
  N7: MOTOR1.YELLOW, BREAKOUT1.YELLOW_wire
  N8: MOTOR1.PINK, BREAKOUT1.PINK_wire
  N9: MOTOR1.BLUE, BREAKOUT1.BLUE_wire

custom parts:
  FRDM-KL25Z: Freedom Board, based on basic pinout of Arduino Rev.3. Attention: the board is NOT 5V compatible.
  ULN2003A breakout board: ULN2003A 7-way Darlington Transistor Driver on breakoutboard
